// Logisim project GshareGiven.circ as structural Verilog: 5 circuits, main circuit main
module main (
);

  wire Clock, Correct, CorrectPred, Done, GsharePredictor_takebranch, InputGen_branchtaken,
       InputGen_isbranch, IsPredBranchCorrect, IsPredCorrect, not_1_out;
  wire [31:0] CorrectPredBranch, GsharePredictor_predbranchdest, InputGen_branchdestaddress, InputGen_predpc,
       InputGen_updatepc;

  InputGen InputGen (
    .Clock(Clock), .PredPC(InputGen_predpc), .UpdatePC(InputGen_updatepc), .IsBranch(InputGen_isbranch),
    .BranchTaken(InputGen_branchtaken), .BranchDestAddress(InputGen_branchdestaddress));
  GsharePredictor GsharePredictor (
    .PredPC(InputGen_predpc), .UpdatePC(InputGen_updatepc), .IsBranch(InputGen_isbranch),
    .BranchTaken(InputGen_branchtaken), .BranchDestAddr(InputGen_branchdestaddress), .Clock(Clock),
    .TakeBranch(GsharePredictor_takebranch), .PredBranchDest(GsharePredictor_predbranchdest));
  Clock clock_1 (.out(Clock));
  Test Test (
    .TakeBranch(GsharePredictor_takebranch), .PredBranchAddress(GsharePredictor_predbranchdest),
    .Clock(Clock), .IsPredCorrect(IsPredCorrect), .CorrectPred(CorrectPred),
    .IsPredBranchCorrect(IsPredBranchCorrect), .CorrectPredBranch(CorrectPredBranch), .Correct(Correct),
    .Done(Done));
  not not_1 (not_1_out, Done);
  Shift_Register #(.length(28)) shift_register_1 (
    .shift(not_1_out), .in(Correct), .clk(Clock));  // open: out, load, clr, d0, q0, d1, q1, d2, q2, d3, q3, d4, q4, d5, q5, d6, q6, d7, q7, d8, q8, d9, q9, d10, q10, d11, q11, d12, q12, d13, q13, d14, q14, d15, q15, d16, q16, d17, q17, d18, q18, d19, q19, d20, q20, d21, q21, d22, q22, d23, q23, d24, q24, d25, q25, d26, q26, d27, q27
  // Probe on IsPredCorrect
  // Probe on CorrectPred
  // Probe on IsPredBranchCorrect
  // Probe on CorrectPredBranch
  // Probe on Correct
  // Probe on Done
endmodule

module GsharePredictor (
  input  [31:0] PredPC,
  input  [31:0] UpdatePC,
  input  IsBranch,
  input  BranchTaken,
  input  [31:0] BranchDestAddr,
  input  Clock,
  output TakeBranch,
  output [31:0] PredBranchDest
);

  wire and_1_out, comparator_1_eq, comparator_1_gt, Counters_Index_____2_n_1, TagRegisters_Index_____PC;
  wire [1:0] BHR, Counter0In, Counter0Out, Counter1In, Counter1Out, Counter2In, Counter2Out, Counter3In,
       Counter3Out, Index, multiplexer_1_out;
  wire [31:0] BDR0Out, BDR1Out, BDR2Out, BDR3Out, multiplexer_2_out, TR0Out, TR1Out, TR2Out, TR3Out;

  Demultiplexer #(.select(2), .width(2), .enable("false")) demultiplexer_1 (
    .out0(Counter0In), .out1(Counter1In), .out2(Counter2In), .out3(Counter3In), .in(2'b01), .sel(Index));
  Shift_Register #(.length(2)) Branch_History_Register (
    .in(BranchTaken), .clk(Clock), .q0(BHR[1]), .q1(BHR[0]));  // open: shift, out, load, clr, d0, d1
  assign Index = PredPC[1:0] ^ BHR;  // XOR_Gate xor_1, 2 bits wide
  Register #(.width(32)) BranchDestinationRegister0 (.Q(BDR0Out), .clk(Clock));  // open: D, en, clr
  Counter #(.width(2), .max('h3), .ongoal("stay")) Counter0 (
    .D(Counter0In), .count(1'b1), .Q(Counter0Out), .clk(Clock));  // open: load, carry, clr
  Register #(.width(32)) TagRegister0 (.Q(TR0Out), .clk(Clock));  // open: D, en, clr
  Register #(.width(32)) TagRegister1 (.Q(TR1Out), .clk(Clock));  // open: D, en, clr
  Register #(.width(32)) BranchDestinationRegister1 (.Q(BDR0Out), .clk(Clock));  // open: D, en, clr
  Multiplexer #(.select(2), .width(2), .enable("false")) multiplexer_1 (
    .in0(Counter0Out), .in1(Counter1Out), .in2(Counter2Out), .in3(Counter3Out), .out(multiplexer_1_out),
    .sel(Index));
  Counter #(.width(2), .max('h3), .ongoal("stay")) Counter1 (
    .D(Counter1In), .count(1'b1), .Q(Counter1Out), .clk(Clock));  // open: load, carry, clr
  Multiplexer #(.select(2), .width(32), .enable("false")) multiplexer_2 (
    .in0(TR0Out), .in1(TR1Out), .in2(TR2Out), .in3(TR3Out), .out(multiplexer_2_out), .sel(Index));
  Register #(.width(32)) TagRegister2 (.Q(TR2Out), .clk(Clock));  // open: D, en, clr
  Multiplexer #(.select(2), .width(32), .enable("false")) multiplexer_3 (
    .in0(BDR0Out), .in1(BDR1Out), .in2(BDR2Out), .in3(BDR3Out), .out(PredBranchDest), .sel(Index));
  Comparator #(.width(2), .mode("unsigned")) comparator_1 (
    .a(multiplexer_1_out), .b(2'b10), .gt(comparator_1_gt), .eq(comparator_1_eq));  // open: lt
  or or_1 (Counters_Index_____2_n_1, comparator_1_gt, comparator_1_eq);
  Counter #(.width(2), .max('h3), .ongoal("stay")) Counter2 (
    .D(Counter2In), .count(1'b1), .Q(Counter2Out), .clk(Clock));  // open: load, carry, clr
  Comparator #(.width(32), .mode("unsigned")) comparator_2 (
    .a(multiplexer_2_out), .b(PredPC), .eq(TagRegisters_Index_____PC));  // open: gt, lt
  Register #(.width(32)) TagRegister3 (.Q(TR3Out), .clk(Clock));  // open: D, en, clr
  Register #(.width(32)) BranchDestinationRegister2 (.Q(BDR0Out), .clk(Clock));  // open: D, en, clr
  Counter #(.width(2), .max('h3), .ongoal("stay")) Counter3 (
    .D(Counter3In), .count(1'b1), .Q(Counter3Out), .clk(Clock));  // open: load, carry, clr
  Register #(.width(32)) BranchDestinationRegister3 (.Q(BDR0Out), .clk(Clock));  // open: D, en, clr
  and and_1 (and_1_out, TakeBranch, TagRegisters_Index_____PC);
  and and_2 (TakeBranch, Counters_Index_____2_n_1, TagRegisters_Index_____PC);

  // Other names for the same wires on the sheet: Branch_Destination_Address[31:0] = PredBranchDest; PC[31:0] = PredPC;
  //   Take_Branch = TakeBranch
endmodule

module InputGen (
  input  Clock,
  output [31:0] PredPC,
  output [31:0] UpdatePC,
  output IsBranch,
  output BranchTaken,
  output [31:0] BranchDestAddress
);

  wire [7:0] counter_1_q;

  Counter #(.max('h1b), .ongoal("stay")) counter_1 (
    .count(1'b1), .Q(counter_1_q), .clk(Clock));  // open: load, D, carry, clr
  ROM #(.dataWidth(32)) rom_1 (.addr(counter_1_q), .data(PredPC));  // open: sel
  ROM #(.dataWidth(1)) rom_2 (.addr(counter_1_q), .data(IsBranch));  // open: sel
  ROM #(.dataWidth(1)) rom_3 (.addr(counter_1_q), .data(BranchTaken));  // open: sel
  ROM #(.dataWidth(32)) rom_4 (.addr(counter_1_q), .data(BranchDestAddress));  // open: sel

  assign UpdatePC = PredPC;

  // Notes on the sheet:
  //   Counter max count is 27 because there are only 28 instructions
  //   contents of rom_1 (hex, n*v repeats v):
  //   5*0 1 1 1 5 2 2 2 3 3 3 0 0 4
  //   contents of rom_2 (hex, n*v repeats v):
  //   8*1 0 8*1 0 10*1
  //   contents of rom_3 (hex, n*v repeats v):
  //   8*1 0 6*1 4*0 1 0 1 0 1 0 1 0 1
  //   contents of rom_4 (hex, n*v repeats v):
  //   5*60 5f 5f 5f 0 5 5 5 8 8 8 60 60 0 10*60
endmodule

module Test (
  input  TakeBranch,
  input  [31:0] PredBranchAddress,
  input  Clock,
  output IsPredCorrect,
  output CorrectPred,
  output IsPredBranchCorrect,
  output [31:0] CorrectPredBranch,
  output Correct,
  output Done
);

  wire comparator_1_eq, comparator_2_eq, DontCare, not_1_out;
  wire [7:0] Count;

  Counter #(.max('h1c), .ongoal("stay")) counter_1 (.count(1'b1), .Q(Count), .clk(Clock));  // open: load, D, carry, clr
  ROM #(.dataWidth(1)) rom_1 (.addr(Count), .data(CorrectPred));  // open: sel
  ROM #(.dataWidth(32)) rom_2 (.addr(Count), .data(CorrectPredBranch));  // open: sel
  ROM #(.dataWidth(1)) rom_3 (.addr(Count), .data(DontCare));  // open: sel
  not not_1 (not_1_out, CorrectPred);
  Comparator #(.width(1), .mode("unsigned")) comparator_1 (
    .a(TakeBranch), .b(CorrectPred), .eq(comparator_1_eq));  // open: gt, lt
  or or_1 (IsPredCorrect, comparator_1_eq, DontCare);
  Comparator #(.width(32), .mode("unsigned")) comparator_2 (
    .a(PredBranchAddress), .b(CorrectPredBranch), .eq(comparator_2_eq));  // open: gt, lt
  Comparator #(.mode("unsigned")) comparator_3 (.a(Count), .b(8'h1c), .eq(Done));  // open: gt, lt
  // Probe on Count
  or or_2 (IsPredBranchCorrect, comparator_2_eq, not_1_out, DontCare);
  and and_1 (Correct, IsPredCorrect, IsPredBranchCorrect);

  // Notes on the sheet:
  //   Correct Take Branch
  //   Correct Prediction Branch Address
  //   Don't Care
  //   contents of rom_1 (hex, n*v repeats v):
  //   4*0 1 0 0 1 0 0 0 1 0 0 1 1 9*0 1 0 1
  //   contents of rom_2 (hex, n*v repeats v):
  //   0 0 0 60 60 0 5f 5f 5f 60 5 5 60 8 8 60 5f 8 8 60 5 7*60
  //   contents of rom_3 (hex, n*v repeats v):
  //   8*0 1 8*0 1
endmodule

module Counters (
  input  _0,
  input  _1,
  input  _2,
  input  _3,
  input  Clock
);

  wire [1:0] Counter0In, Counter0Out, Counter1In, Counter1Out, Counter2In, Counter2Out, Counter3Out;

  Counter #(.width(2), .max('h3), .ongoal("stay")) Zero (
    .D(Counter0In), .count(1'b1), .Q(Counter0Out), .clk(Clock));  // open: load, carry, clr
  Counter #(.width(2), .max('h3), .ongoal("stay")) One (
    .D(Counter1In), .count(1'b1), .Q(Counter1Out), .clk(Clock));  // open: load, carry, clr
  Counter #(.width(2), .max('h3), .ongoal("stay")) Two (
    .D(Counter2In), .count(1'b1), .Q(Counter2Out), .clk(Clock));  // open: load, carry, clr
  Counter #(.width(2), .max('h3), .ongoal("stay")) Three (
    .D(Counter2In), .count(1'b1), .Q(Counter3Out), .clk(Clock));  // open: load, carry, clr

  // Other names for the same wires on the sheet: Counter0 = _0; Counter1 = _1; Counter2 = _2; Counter3 = _3
endmodule
